# Fritzing sketch flow-meter-sketch (saved by Fritzing 0.9.4)
breadboards: 1

parts:
  Bauteil1 = Arduino Nano (Rev3.0)
  Bauteil2 = Arduino Leonardo (Rev3b)
  C1 = Capacitor [package=cap-pth-small-kit]
  R1 = Resistor [tolerance=±5% resistance=10k package=THT]
  R2 = Resistor [tolerance=±5% resistance=10k package=THT]

nets:
  GND: Bauteil1.GND, Bauteil2.GND, C1.1
  N1: Bauteil1.A5, Bauteil2.D3_PWM/SCL, R2.Pin_0
  N2: Bauteil1.A4, Bauteil2.D2/SDA, R1.Pin_0
  N3: Bauteil2.5V, C1.2, R1.Pin_1, R2.Pin_1

notes:
  Sensor
  Controller
  Digital interface (I2C)
  - SCL
  - SDA
  - GND
  Analog interface (I2C)
  to differential pressure sensor
  - VCC (+5V)
  - GND
  - Analog input
